# Fritzing sketch XTone Rebuild (saved by Fritzing 0.9.10b)
breadboards: 1

parts:
  SA = Round Pushbutton
  SB = Round Pushbutton
  SC = Round Pushbutton
  SD = Round Pushbutton
  SE = Round Pushbutton
  SF = Round Pushbutton
  Part2 = Adafruit MIDI FeatherWing Kit [part_number=ADA4740]
  Mod1 = Raspberry Pi Pico
  EXP = AMPHENOL - ACJS-MHDR [package=ACJS-MHDR]
  RE1 = KY-040 Rotary encoder [package=THT]
  RE2 = KY-040 Rotary encoder [package=THT]

nets:
  GND: SA.leg0, SB.leg0, SC.leg0, Part2.GND, Mod1.pin_3, Mod1.pin_8, Mod1.pin_13, Mod1.pin_18, Mod1.pin_23, Mod1.pin_28, Mod1.pin_33, Mod1.pin_38, Mod1.pin_42, EXP.Sleeve_(1), RE1.GND, RE2.GND
  N1: SA.leg1, Mod1.pin_10
  N2: SB.leg1, Mod1.pin_9
  N3: SC.leg1, Mod1.pin_7
  N4: SD.leg1, Mod1.pin_6
  N5: SE.leg1, Mod1.pin_5
  N6: SF.leg1, Mod1.pin_4
  VCC: Part2.3.3V, Mod1.pin_36, EXP.Tip_(3), RE1.Vcc, RE2.Vcc
  N7: Part2.MIDI_RX, Mod1.pin_2
  N8: Part2.MIDI_TX, Mod1.pin_1
  N9: Mod1.pin_21, RE2.CLK
  N10: Mod1.pin_22, RE2.DT
  N11: Mod1.pin_24, RE2.SW
  N12: Mod1.pin_25, RE1.CLK
  N13: Mod1.pin_26, RE1.DT
  N14: Mod1.pin_27, RE1.SW
  N15: Mod1.pin_34, EXP.Ring_(2)

custom parts:
  Adafruit MIDI FeatherWing Kit: Turn your Feather into a song-bird with this musically-enabled FeatherWing that adds MIDI input and output jacks to just about any Feather. You get both input and output DIN-5 MIDI jacks, a 3V optically isolator so you can interface with MIDI on 3.3V logic/power microcontrollers, and two blinky indicator LEDs underneath the jacks to help you know when data is sent and received. For those who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
  Raspberry Pi Pico: Raspberry Pi Pico. Based around the RP2040 microcontroller the Pico is a low cost microcontroller device bringing Raspberry Pi quality, cost, and easy of use to the microcontroller space. Jan 2021, Split part in to two versions: tht (this one) and SMD. This one will drill holes for a .1 in header in pcb to allow plugging in the module as well as providing pads to solder the module to the top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
  KY-040 Rotary encoder: KY-040 Rotary Encoder with switch on breakout borad from AZ Delivery
